// Logisim project pc.circ as structural Verilog: 1 circuit, main circuit PC
module PC (
  input  [31:0] Input,
  input  Clk,
  output [31:0] Output
);

  Register #(.width(32)) PC (.D(Input), .en(1'b1), .Q(Output), .clk(Clk), .clr(1'b0));
endmodule
