// Logisim project regfile.circ as structural Verilog: 2 circuits, main circuit RegFile
module RegFile (
  input  [4:0] RD,
  input  [4:0] RS1,
  input  [4:0] RS2,
  input  [31:0] W,
  input  WE,
  input  Clk,
  output [31:0] s0,
  output [31:0] s1,
  output [31:0] t0,
  output [31:0] t1,
  output [31:0] a0,
  output [31:0] a1,
  output [31:0] ra,
  output [31:0] sp,
  output [31:0] R1,
  output [31:0] R2
);

  wire we_a0, we_a1, we_ra, we_s0, we_s1, we_sp, we_t0, we_t1;

  Demultiplexer #(.select(5)) demultiplexer_1 (
    .out1(we_ra), .out2(we_sp), .out5(we_t0), .out6(we_t1), .out8(we_s0), .out9(we_s1), .out10(we_a0),
    .out11(we_a1), .in(WE), .sel(RD));  // open: out0, out3, out4, out7, out12, out13, out14, out15, out16, out17, out18, out19, out20, out21, out22, out23, out24, out25, out26, out27, out28, out29, out30, out31, en
  Register #(.width(32)) register_1 (.D(W), .en(we_s0), .Q(s0), .clk(Clk));  // open: clr
  Register #(.width(32)) register_2 (.D(W), .en(we_s1), .Q(s1), .clk(Clk));  // open: clr
  Register #(.width(32)) register_3 (.D(W), .en(we_t0), .Q(t0), .clk(Clk));  // open: clr
  Register #(.width(32)) register_4 (.D(W), .en(we_t1), .Q(t1), .clk(Clk));  // open: clr
  Register #(.width(32)) register_5 (.D(W), .en(we_a0), .Q(a0), .clk(Clk));  // open: clr
  Register #(.width(32)) register_6 (.D(W), .en(we_ra), .Q(ra), .clk(Clk));  // open: clr
  Register #(.width(32)) register_7 (.D(W), .en(we_sp), .Q(sp), .clk(Clk));  // open: clr
  Register #(.width(32)) register_8 (.D(W), .en(we_a1), .Q(a1), .clk(Clk));  // open: clr

  // Notes on the sheet:
  //   Write Register
  //   Read Register 1
  //   Read Register 2
  //   Write Data
  //   Write Enable
  //   Clock
  //   NOTE
  //   x1:ra
  //   x2 : sp
  //   x5,x6: t0,t1
  //   x8,x9: s0,s1
  //   x10,x11:a0,a1
  //   Please do not modify/replace/move/change/delete/etc input and output pins
  //   Creo que este siempre deberia ser WE
  //   These are debug/test outputs from your circuit
  //   Read Data 1
  //   Read Data 2
endmodule

module generic_register (
);

  Register #(.width(32)) register_1 ();  // open: D, en, Q, clk, clr
endmodule
