// Logisim project riscv.circ as structural Verilog: 1 circuit, main circuit RISC-V
module RISC_V (
  input  in_1,
  input  in_2,
  output [31:0] s0,
  output [31:0] s1,
  output [31:0] t0,
  output [31:0] t1,
  output [31:0] a0,
  output [31:0] ra,
  output [31:0] sp,
  output [15:0] Time_Step,
  output [31:0] out_11,
  output [31:0] out_12
);

  wire clk;

  Counter #(.width(16), .max('hffff)) counter_1 (.Q(Time_Step), .clk(clk));  // open: load, D, count, carry, clr
  // CPU cpu_1: pin names not known; wires that end beside it: out_12, s0, clk, s1, in_1, t0, in_2, t1, a0, ra, sp, out_11
  Clock clock_1 (.out(clk));
  // Probe on out_11
  // RISC_VProgramROM risc_vprogramrom_1: pin names not known; wires that end beside it: out_11, out_12
  // Probe on out_12

  // Other names for the same wires on the sheet: fetch_addr[31:0] = out_11; instruction[31:0] = out_12

  // Notes on the sheet:
  //   These are debug/test outputs from your circuit
endmodule
